# Fritzing sketch Garage_Frirtzing (saved by Fritzing 0.9.3b)
breadboards: 3

parts:
  U1 = ATMEGA32U4 [package=qfn]
  Matrix_keypad1 = KEYPAD 4x4  # not connected
  LCD1 = LCD screen
  R1 = Resistor [tolerance=±5% resistance=220 package=THT]
  LED1 = LED - 5mm [color="Red (633nm)" package="5 mm [THT]"]
  M2 = DC Motor
  RY2 = srd-05vdc-sl-c
  Q3 = NPN-Transistor [package="TO92 [THT]"]
  LED2 = LED - 5mm [color="Red (633nm)" package="5 mm [THT]"]
  Q4 = NPN-Transistor [package="TO92 [THT]"]
  R8 = Resistor [tolerance=±5% resistance=1k package=THT]
  D2 = Rectifier Diode [part_number=1N4001 package="300 mil [THT]"]
  BAT2 = BC9VPC [package=bc9vpc]
  R9 = Resistor [tolerance=±5% resistance=220 package=THT]
  R12 = Trimmer Potentiometer [maximum_resistance=10kΩ package=THT]
  U6 = Optocoupler [package=THT]

nets:
  N1: U1.GND, LCD1.DB6
  N2: U1.PD4(ADC8), Q3.B
  N3: U1.VCC, LCD1.DB7
  N4: U1.PF7(ADC7), LCD1.DB5
  N5: U1.PF6(ADC6), LCD1.DB4
  N6: U1.PF5(ADC5), LCD1.E
  N7: U1.PF4(ADC4), LCD1.RS
  N8: LCD1.VSS, LCD1.R/W, LCD1.LED-, R12.leg2
  N9: LCD1.VDD, LCD1.LED+, R12.leg1
  N10: LCD1.V0, R12.wiper
  N11: R1.Pin_1, LED1.anode
  N12: M2.pin_1, RY2.pin_2
  N13: M2.pin_2, RY2.pin_4, D2.cathode, BAT2.V+, U6.Pin_5
  N14: RY2.pin_5, LED2.cathode, Q4.E, BAT2.V-
  N15: Q3.E, U6.Pin_1
  N16: LED2.anode, R9.Pin_0
  N17: Q4.B, R8.Pin_1
  N18: Q4.C, D2.anode
  N19: R8.Pin_0, U6.Pin_4
  N20: R9.Pin_1, U6.Pin_2

custom parts:
  KEYPAD 4x4: Matrix keypad 16 buttons, 4 rows x 4 columns
